# Fritzing sketch ttn_node_water_flow (saved by Fritzing 0.9.4)

parts:
  YF-S201_Flow_Meter1 = YF-S201 Water Flow Meter
  5V_DC_to_3_3V_DC = DC_DC_XL4016 [package=board_screw]
  Mod2 = Heltec CubeCell Dev-Board [part_number=HTCC-AB01]
  5V_DC = 2.1mm Barrel Jack with Terminal Block

nets:
  N1: YF-S201_Flow_Meter1.SIG, 5V_DC_to_3_3V_DC.OUT-, Mod2.pin_11, Mod2.pin_14
  N2: YF-S201_Flow_Meter1.GND, Mod2.pin_21
  N3: YF-S201_Flow_Meter1.VCC, 5V_DC_to_3_3V_DC.IN+, 5V_DC.POS
  N4: 5V_DC_to_3_3V_DC.IN-, 5V_DC.NEG

custom parts:
  YF-S201 Water Flow Meter: The YF-S201 Flow Meter. The input voltage is 5V to 24V (DC).
  Heltec CubeCell Dev-Board: CubeCell is a part of the Heltec LoRa series and incorporates a PSoC 4000 series processor and SX1262 RF transceiver with an integrated CP2102 USB to serial port interface and onboard SHT1.25 battery interface with integrated lithium battery management system, supporting direct solar panel connection. Links: Heltec CubeCell Dev-Board product page Github
